# Fritzing sketch Circuito (saved by Fritzing 0.9.3b)
breadboards: 1

parts:
  Raspberry_Pi_1 = Raspberry Pi 3 [part_number=RPI-3-V1.2]
  U1 = 2-Channel 5v Relay Shield [package=relay-2ch5v10a]
  F1 = Fan - Ventilador [package=THT]
  hc-sr1 = hc-sr04
  R1 = Resistor [tolerance=±5% resistance=1k package="0805 [SMD]"]
  R2 = Resistor [tolerance=±5% resistance=2.2k package="0805 [SMD]"]

nets:
  GND: Raspberry_Pi_1.GND, U1.GND, F1.GND, hc-sr1.GND, R2.Pin_1
  N1: Raspberry_Pi_1.GPIO17, U1.IN1
  N2: Raspberry_Pi_1.GPIO24, R1.Pin_1, R2.Pin_0
  N3: Raspberry_Pi_1.GPIO23, hc-sr1.Trig
  5V: Raspberry_Pi_1.5V, U1.VCC, F1.5V, hc-sr1.VCC
  N4: hc-sr1.Echo, R1.Pin_0

notes:
  Electroimán
  Fuente 12V
  Led RGB
  Botón No Touch
  Cámara IR
  Parlante

custom parts:
  2-Channel 5v Relay Shield: 2 Channel 5v Relay Shield w. 2x SPD-06VDC-SD-C
  Fan - Ventilador: Ventilador de 2 pines, se encuentra comunmente en computadoras de escritorio
